# Fritzing sketch sketch (saved by Fritzing 0.7.11b)
breadboards: 1

parts:
  Arduino1 = Arduino
  S1 = Pushbutton [package=THT]
  S2 = Pushbutton [package=THT]
  S3 = Pushbutton [package=THT]
  S4 = Pushbutton [package=THT]
  S5 = Pushbutton [package=THT]
  LED1 = LED - 5mm [color="Red (633nm)" package="5 mm [THT]"]
  LED2 = LED - 5mm [color="Red (633nm)" package="5 mm [THT]"]
  LED3 = LED - 5mm [color="Red (633nm)" package="5 mm [THT]"]
  LED4 = LED - 5mm [color="Red (633nm)" package="5 mm [THT]"]
  LED5 = LED - 5mm [color="Red (633nm)" package="5 mm [THT]"]
  1_5kΩ = Resistor [tolerance=±5% resistance=1.5k package=THT]
  J1 = Piezo Speaker
  100Ω = Resistor [tolerance=±5% resistance=100 package=THT]
  S6 = Toggle Switch [package=THT]
  9V = Battery block 9V

nets:
  GND: Arduino1.GND, S1.leg1, S2.leg1, S3.leg1, S4.leg1, S5.leg1, 1_5kΩ.Pin_0, 100Ω.Pin_1, 9V.-
  N1: Arduino1.D9, J1.pin1
  N2: Arduino1.D4, LED5.anode
  N3: Arduino1.D3, LED4.anode
  N4: Arduino1.D2, LED3.anode
  N5: Arduino1.D1TX, LED2.anode
  N6: Arduino1.D0RX, LED1.anode
  N7: Arduino1.VIN, S6.L1
  N8: Arduino1.A0, S1.leg0
  N9: Arduino1.A1, S2.leg0
  N10: Arduino1.A2, S3.leg0
  N11: Arduino1.A3, S4.leg0
  N12: Arduino1.A4, S5.leg0
  N13: LED1.cathode, LED2.cathode, LED3.cathode, LED4.cathode, LED5.cathode, 1_5kΩ.Pin_1
  N14: J1.pin2, 100Ω.Pin_0
  N15: S6.COM, 9V.+
