# Fritzing sketch sketch2 (saved by Fritzing 0.7.11b)
breadboards: 1

parts:
  Arduino1 = Arduino
  LED1 = LED - 5mm [color="Red (633nm)" package="5 mm [THT]"]
  LED2 = LED - 5mm [color="Red (633nm)" package="5 mm [THT]"]
  LED3 = LED - 5mm [color="Red (633nm)" package="5 mm [THT]"]
  LED4 = LED - 5mm [color="Red (633nm)" package="5 mm [THT]"]
  LED5 = LED - 5mm [color="Red (633nm)" package="5 mm [THT]"]
  1_5kΩ = Resistor [tolerance=±5% resistance=1.5k package=THT]
  speaker = Piezo Speaker
  100Ω = Resistor [tolerance=±5% resistance=100 package=THT]
  S6 = Toggle Switch [package=THT]
  J2 = Screw terminal - 2 pins [package=THT]
  S4 = Pushbutton [package="[THT]"]
  S2 = Pushbutton [package="[THT]"]
  S3 = Pushbutton [package="[THT]"]
  S1 = Pushbutton [package="[THT]"]
  S5 = Pushbutton [package="[THT]"]

nets:
  GND: Arduino1.GND, 1_5kΩ.Pin_0, 100Ω.Pin_1, J2.pin2, S4.Pin_3, S4.Pin_4, S2.Pin_3, S2.Pin_4, S3.Pin_3, S3.Pin_4, S1.Pin_3, S1.Pin_4, S5.Pin_3, S5.Pin_4
  N1: Arduino1.D9, speaker.pin1
  N2: Arduino1.D4, LED5.anode
  N3: Arduino1.D3, LED4.anode
  N4: Arduino1.D2, LED3.anode
  N5: Arduino1.D1TX, LED2.anode
  N6: Arduino1.D0RX, LED1.anode
  N7: Arduino1.VIN, S6.L1
  N8: Arduino1.A0, S5.Pin_1, S5.Pin_2
  N9: Arduino1.A1, S4.Pin_1, S4.Pin_2
  N10: Arduino1.A2, S3.Pin_1, S3.Pin_2
  N11: Arduino1.A3, S2.Pin_1
  N12: Arduino1.A4, S1.Pin_1, S1.Pin_2
  N13: LED1.cathode, LED2.cathode, LED3.cathode, LED4.cathode, LED5.cathode, 1_5kΩ.Pin_1
  N14: speaker.pin2, 100Ω.Pin_0
  N15: S6.COM, J2.pin1

notes:
  Vin
  GND
