# Fritzing sketch sketch_battery (saved by Fritzing 0.7.11b)
breadboards: 1

parts:
  Arduino1 = Arduino
  LED1 = LED - 5mm [color="Red (633nm)" package="5 mm [THT]"]
  LED2 = LED - 5mm [color="Red (633nm)" package="5 mm [THT]"]
  LED3 = LED - 5mm [color="Red (633nm)" package="5 mm [THT]"]
  LED4 = LED - 5mm [color="Red (633nm)" package="5 mm [THT]"]
  LED5 = LED - 5mm [color="Red (633nm)" package="5 mm [THT]"]
  R1 = Resistor [tolerance=±5% resistance=1.5k package=THT]
  S1 = Pushbutton [package="[THT]"]
  S2 = Pushbutton [package="[THT]"]
  S3 = Pushbutton [package="[THT]"]
  S4 = Pushbutton [package="[THT]"]
  S5 = Pushbutton [package="[THT]"]
  J1 = Piezo Speaker
  R2 = Resistor [tolerance=±5% resistance=100 package=THT]
  S6 = Toggle Switch [package=THT]
  VCC1 = Battery block 9V

nets:
  N1: Arduino1.D6, J1.pin1
  N2: Arduino1.D4, LED2.anode
  N3: Arduino1.D3, LED1.anode
  N4: Arduino1.D2, LED3.anode
  N5: Arduino1.D1TX, LED4.anode
  N6: Arduino1.D0RX, LED5.anode
  N7: Arduino1.GND, R1.Pin_0, S1.Pin_2, S2.Pin_1, S2.Pin_2, S3.Pin_1, S3.Pin_2, S4.Pin_2, S5.Pin_2, R2.Pin_0, VCC1.-
  N8: Arduino1.VIN, S6.L1
  N9: Arduino1.A0, S2.Pin_3, S2.Pin_4
  N10: Arduino1.A1, S3.Pin_3, S3.Pin_4
  N11: Arduino1.A2, S4.Pin_3, S4.Pin_4
  N12: Arduino1.A3, S5.Pin_3, S5.Pin_4
  N13: Arduino1.A4, S1.Pin_3, S1.Pin_4
  N14: J1.pin2, R2.Pin_1
  N15: S6.COM, VCC1.+
