# Fritzing sketch sketch_leds (saved by Fritzing 0.7.11b)
breadboards: 1

parts:
  Arduino1 = Arduino
  LED1 = LED - 5mm [color="Red (633nm)" package="5 mm [THT]"]
  LED2 = LED - 5mm [color="Red (633nm)" package="5 mm [THT]"]
  LED3 = LED - 5mm [color="Red (633nm)" package="5 mm [THT]"]
  LED4 = LED - 5mm [color="Red (633nm)" package="5 mm [THT]"]
  LED5 = LED - 5mm [color="Red (633nm)" package="5 mm [THT]"]
  R1 = Resistor [tolerance=±5% resistance=1.5k package=THT]

nets:
  N1: Arduino1.D4, LED2.anode
  N2: Arduino1.D3, LED1.anode
  N3: Arduino1.D2, LED3.anode
  N4: Arduino1.D1TX, LED4.anode
  N5: Arduino1.D0RX, LED5.anode
  N6: Arduino1.GND, R1.Pin_0
